# Fritzing sketch frog2 (saved by Fritzing 0.8.7b)
breadboards: 1

parts:
  M4 = Stepper Motor - Bipolar
  J3 = Basic Servo
  J4 = Basic Servo
  M5 = DC Motor
  M6 = DC Motor
  Componente4 = SRF05 Ultrasonic Rangefinder
  IR2 = TSOP312.., 314.. [package=THT]
  S2 = Pushbutton [package=THT]
  Componente5 = Arduino Mega 2560 (Rev3)

nets:
  N1: M4.A, Componente5.D50
  N2: M4.C, Componente5.D51
  N3: M4.B, Componente5.D52
  N4: M4.D, Componente5.D53
  GND: J3.gnd, J4.gnd, S2.leg0
  VCC: J3.vcc, J4.vcc
  N5: M5.pin_1, Componente5.D9_PWM
  N6: M5.pin_2, Componente5.D6_PWM
  N7: M6.pin_1, Componente5.D11_PWM
  N8: M6.pin_2, Componente5.D10_PWM
  N9: Componente4.VCC, IR2.Vs
  N10: Componente4.Trig, Componente5.D48
  N11: Componente4.Echo, Componente5.D49
  GND_2: Componente4.GND, IR2.GND

notes:
  Motor CD-ROM
