# Fritzing sketch robo (saved by Fritzing 0.9.2b)
breadboards: 1

parts:
  Componente1 = Arduino Mega 2560 (Rev3)
  S1 = H-Bridge with L298N
  MotorD = DC Motor
  MotorE = DC Motor

nets:
  N1: Componente1.D11_PWM, S1.IN1
  N2: Componente1.D10_PWM, S1.IN2
  N3: Componente1.D9_PWM, S1.IN3
  N4: Componente1.D8_PWM, S1.IN4
  5V: Componente1.5V, S1.12V
  GND: Componente1.GND, S1.GND
  N5: S1.M1-01, MotorE.pin_2
  N6: S1.M1-02, MotorE.pin_1
  N7: S1.M2-01, MotorD.pin_2
  N8: S1.M2-02, MotorD.pin_1

custom parts:
  H-Bridge with L298N: h-bridge
